// Logisim project EveryThing.circ as structural Verilog: 1 circuit, main circuit main
module main (
  input  in_1,
  input  in_2,
  input  in_3,
  input  SR_Flip_Flop,
  input  in_5,
  input  [15:0] in_6,
  input  in_7,
  input  [15:0] in_8,
  input  in_9,
  input  in_10,
  input  in_11,
  input  in_12,
  input  in_13,
  input  [2:0] in_14,
  input  in_15,
  input  Data_Flip_Flop,
  input  [14:0] in_17,
  input  in_18,
  input  Full_Adder,
  input  in_20,
  input  in_21,
  input  in_22,
  input  in_23,
  input  in_24,
  input  in_25,
  input  in_26,
  input  in_27,
  input  in_28,
  input  [1:0] _2_bit_Adder,
  input  [1:0] in_30,
  input  [15:0] in_31,
  input  in_32,
  input  in_33,
  input  DeMux,
  input  [3:0] in_35,
  input  [3:0] in_36,
  input  [15:0] in_37,
  input  in_38,
  input  in_39,
  input  [15:0] in_40,
  input  in_41,
  input  [15:0] in_42,
  input  [15:0] in_43,
  input  in_44,
  input  in_45,
  input  [5:0] in_46,
  input  [15:0] in_47,
  input  [15:0] in_48,
  input  in_49,
  input  in_50,
  input  [15:0] in_51,
  input  [15:0] in_52,
  input  in_53,
  input  in_54,
  input  in_55,
  input  in_56,
  input  [15:0] in_57,
  input  [15:0] in_58,
  input  [15:0] in_59,
  input  in_60,
  input  in_61,
  input  in_62,
  input  in_63
);

  wire adder_3_cout, adder_4_cout, adder_5_cout, adder_5_out, adder_6_cout, adder_7_cout, and_1_out,
       and_2_out, and_3_out, and_4_out, and_5_out, and_6_out, and_7_out, and_9_out, and_10_out, and_11_out,
       and_12_out, and_13_out, clock_1_out, clock_2_out, clock_3_out, clock_4_out, clock_5_out, clock_6_out,
       clock_7_out, clock_8_out, d_ff_1_q, demultiplexer_2_out0, demultiplexer_2_out1, demultiplexer_5_out0,
       demultiplexer_5_out1, demultiplexer_5_out2, demultiplexer_5_out3, demultiplexer_5_out4,
       demultiplexer_5_out5, demultiplexer_5_out6, demultiplexer_5_out7, demultiplexer_6_out0,
       demultiplexer_6_out1, demultiplexer_6_out2, demultiplexer_6_out3, demultiplexer_6_out4,
       demultiplexer_6_out5, demultiplexer_6_out6, demultiplexer_6_out7, demultiplexer_7_out0,
       demultiplexer_7_out1, demultiplexer_8_out0, demultiplexer_8_out1, ledbar_10_p2, ledbar_13_p1,
       multiplexer_1_out, multiplexer_12_out, nand_1_out, nand_2_out, nand_3_out, nand_4_out, nand_5_out,
       nand_6_out, nand_7_out, nand_8_out, nand_9_out, nand_10_out, nand_11_out, nand_12_out, nand_13_out,
       nand_14_out, nand_15_out, nand_16_out, nand_17_out, nand_18_out, nand_19_out, nand_20_out,
       nand_21_out, nand_22_out, nand_23_out, not_1_out, not_2_out, not_7_out, not_8_out, not_9_out,
       not_10_out, or_2_out, or_3_out, or_4_out, or_5_out, or_6_out, or_7_out, or_8_out, or_9_out, or_10_out,
       or_11_out, or_12_out, or_13_out, or_14_out, or_15_out, or_16_out, or_17_out, or_18_out, or_19_out,
       or_20_out, or_21_out, or_22_out, or_23_out, or_24_out, or_25_out, or_26_out, or_27_out, or_28_out,
       or_29_out, or_30_out, or_31_out, or_32_out, or_33_out, or_34_out, or_35_out, or_36_out, or_37_out,
       or_38_out, or_39_out, or_40_out, xor_2_out, xor_3_out, xor_4_out;
  wire [1:0] adder_3_out;
  wire [3:0] adder_7_out;
  wire [14:0] ledbar_17_p1;
  wire [15:0] adder_8_out, adder_9_out, adder_10_out, and_8_out, and_15_out, counter_1_q,
       demultiplexer_1_out0, demultiplexer_1_out1, demultiplexer_3_out0, demultiplexer_3_out1,
       demultiplexer_4_out0, demultiplexer_4_out1, ledbar_8_p1, ledbar_9_p2, ledbar_11_p1, ledbar_12_p1,
       ledbar_14_p1, ledbar_15_p1, multiplexer_2_out, multiplexer_3_out, multiplexer_4_out,
       multiplexer_5_out, multiplexer_6_out, multiplexer_7_out, multiplexer_8_out, multiplexer_9_out,
       multiplexer_11_out, multiplexer_13_out, multiplexer_14_out, multiplexer_17_out, multiplexer_18_out,
       multiplexer_19_out, multiplexer_20_out, multiplexer_21_out, multiplexer_22_out, multiplexer_24_out,
       multiplexer_25_out, not_4_out, not_5_out, not_6_out, not_11_out, not_12_out, not_13_out, ram_1_dout,
       ram_2_dout, ram_3_dout, ram_4_dout, ram_5_dout, ram_6_dout, ram_7_dout, ram_8_dout, ram_9_dout,
       ram_10_dout, register_17_q, register_18_q, register_19_q, register_20_q, register_21_q, register_22_q,
       register_23_q, register_24_q, register_25_q, register_26_q, register_28_q;
  wire [15:15] register_27_q;

  nand nand_1 (nand_1_out, in_1, in_5);
  nand nand_2 (nand_2_out, in_7, in_7);
  nand nand_3 (nand_3_out, in_12, in_12);
  nand nand_4 (nand_4_out, in_15, in_15);
  not not_1 (not_1_out, DeMux);
  Demultiplexer #(.width(16)) demultiplexer_1 (
    .out0(demultiplexer_1_out0), .out1(demultiplexer_1_out1), .in(in_58), .sel(in_53));
  nand nand_5 (nand_5_out, nand_1_out, nand_1_out);
  LED led_1 (.in(nand_2_out));
  nand nand_6 (nand_6_out, in_21, in_21);
  nand nand_7 (nand_7_out, in_22, in_22);
  and and_1 (and_1_out, in_24, not_2_out);
  not not_2 (not_2_out, in_26);
  and and_2 (and_2_out, in_25, in_26);
  Multiplexer multiplexer_1 (.in0(in_24), .in1(in_25), .out(multiplexer_1_out), .sel(in_26));
  and and_3 (and_3_out, in_33, not_1_out);
  LED led_2 (.in(and_3_out));
  and and_4 (and_4_out, in_33, DeMux);
  LED led_3 (.in(and_4_out));
  LED led_4 (.in(demultiplexer_2_out0));
  Demultiplexer demultiplexer_2 (.out0(demultiplexer_2_out0), .out1(demultiplexer_2_out1), .in(in_33), .sel(DeMux));
  LED led_5 (.in(demultiplexer_2_out1));
  Multiplexer #(.width(16)) multiplexer_2 (.in0(in_40), .in1(in_42), .out(multiplexer_2_out), .sel(in_39));
  Multiplexer #(.width(16)) multiplexer_3 (.in0(in_43), .in1(in_48), .out(multiplexer_3_out), .sel(in_39));
  Demultiplexer #(.width(16)) demultiplexer_3 (
    .out0(demultiplexer_3_out0), .out1(demultiplexer_3_out1), .in(demultiplexer_1_out0), .sel(in_54));
  Demultiplexer #(.width(16)) demultiplexer_4 (
    .out0(demultiplexer_4_out0), .out1(demultiplexer_4_out1), .in(demultiplexer_1_out1), .sel(in_54));
  LED led_6 (.in(nand_5_out));
  // NOT_Gate not_3 is placed but not wired
  nand nand_8 (nand_8_out, nand_3_out, nand_4_out);
  LED led_7 (.in(nand_8_out));
  nand nand_9 (nand_9_out, nand_6_out, in_22);
  nand nand_10 (nand_10_out, nand_7_out, in_21);
  LED led_8 (.in(multiplexer_1_out));
  Multiplexer #(.width(16)) multiplexer_4 (
    .in0(multiplexer_2_out), .in1(multiplexer_3_out), .out(multiplexer_4_out), .sel(in_38));
  // LedBar #(.inputtype("row"), .matrixcols(16)) ledbar_1: pin names not known; wires that end beside it: multiplexer_4_out
  // LedBar #(.inputtype("row"), .matrixcols(16)) ledbar_2: pin names not known; wires that end beside it: demultiplexer_3_out0
  // LedBar #(.inputtype("row"), .matrixcols(16)) ledbar_3: pin names not known; wires that end beside it: in_54, demultiplexer_3_out1
  // LedBar #(.inputtype("row"), .matrixcols(16)) ledbar_4: pin names not known; wires that end beside it: demultiplexer_4_out0
  // LedBar #(.inputtype("row"), .matrixcols(16)) ledbar_5: pin names not known; wires that end beside it: demultiplexer_4_out1
  // OR_Gate or_1 is placed but not wired
  nand nand_11 (nand_11_out, nand_9_out, nand_9_out);
  nand nand_12 (nand_12_out, nand_10_out, nand_10_out);
  nand nand_13 (nand_13_out, nand_11_out, nand_11_out);
  nand nand_14 (nand_14_out, nand_12_out, nand_12_out);
  or or_2 (or_2_out, and_1_out, and_2_out);
  LED led_9 (.in(or_2_out));
  nand nand_15 (nand_15_out, nand_13_out, nand_14_out);
  LED led_10 (.in(nand_15_out));
  // XOR_Gate xor_1 is placed but not wired
  Adder #(.width(1)) adder_1 (
    .a(_2_bit_Adder[1]), .b(in_30[1]), .out(adder_3_out[1]), .cin(adder_3_cout));  // open: cout
  Adder #(.width(1)) adder_2 (.a(in_35[3]), .b(in_36[3]), .out(adder_7_out[3]), .cin(adder_4_cout));  // open: cout
  xor xor_2 (xor_2_out, in_2, in_3);
  and and_5 (and_5_out, in_3, in_2);
  xor xor_3 (xor_3_out, in_18, in_20);
  Adder #(.width(1)) adder_3 (
    .a(_2_bit_Adder[0]), .b(in_30[0]), .out(adder_3_out[0]), .cout(adder_3_cout));  // open: cin
  // LedBar #(.inputtype("row"), .matrixcols(2)) ledbar_6: pin names not known; wires that end beside it: adder_3_out
  Adder #(.width(1)) adder_4 (
    .a(in_35[2]), .b(in_36[2]), .out(adder_7_out[2]), .cin(adder_6_cout), .cout(adder_4_cout));
  Multiplexer #(.width(16)) multiplexer_5 (.in0(in_47), .in1({16{1'b0}}), .out(multiplexer_5_out), .sel(in_44));
  Multiplexer #(.width(16)) multiplexer_6 (.in0(in_51), .in1({16{1'b0}}), .out(multiplexer_6_out), .sel(in_56));
  or or_3 (or_3_out, 1'b0, ledbar_8_p1[15]);
  LED led_11 (.in(xor_2_out));
  LED led_12 (.in(and_5_out));
  Adder #(.width(1)) adder_5 (.a(in_10), .b(in_9), .out(adder_5_out), .cout(adder_5_cout));  // open: cin
  LED led_13 (.in(adder_5_out));
  LED led_14 (.in(adder_5_cout));
  and and_6 (and_6_out, xor_3_out, Full_Adder);
  and and_7 (and_7_out, in_18, in_20);
  Adder #(.width(1)) adder_6 (
    .a(in_35[1]), .b(in_36[1]), .out(adder_7_out[1]), .cin(adder_7_cout), .cout(adder_6_cout));
  Multiplexer #(.width(16)) multiplexer_7 (
    .in0(multiplexer_5_out), .in1(not_4_out), .out(multiplexer_7_out), .sel(in_45));
  assign not_4_out = ~multiplexer_5_out;  // NOT_Gate not_4, 16 bits wide
  Multiplexer #(.width(16)) multiplexer_8 (
    .in0(multiplexer_6_out), .in1(not_5_out), .out(multiplexer_8_out), .sel(in_55));
  assign not_5_out = ~multiplexer_6_out;  // NOT_Gate not_5, 16 bits wide
  or or_4 (or_4_out, ledbar_8_p1[15], ledbar_8_p1[14]);
  or or_5 (or_5_out, or_4_out, ledbar_8_p1[13]);
  xor xor_4 (xor_4_out, xor_3_out, Full_Adder);
  LED led_15 (.in(xor_4_out));
  or or_6 (or_6_out, and_6_out, and_7_out);
  LED led_16 (.in(or_6_out));
  Adder #(.width(1)) adder_7 (.a(in_35[0]), .b(in_36[0]), .out(adder_7_out[0]), .cout(adder_7_cout));  // open: cin
  // LedBar #(.inputtype("row"), .matrixcols(4)) ledbar_7: pin names not known; wires that end beside it: adder_7_out
  // LedBar #(.inputtype("row"), .matrixcols(16)) ledbar_8: pin names not known; wires that end beside it: ledbar_8_p1
  assign and_8_out = multiplexer_7_out & multiplexer_8_out;  // AND_Gate and_8, 16 bits wide
  Adder #(.width(16)) adder_8 (.a(multiplexer_7_out), .b(multiplexer_8_out), .out(adder_8_out));  // open: cin, cout
  or or_7 (or_7_out, or_5_out, ledbar_8_p1[12]);
  or or_8 (or_8_out, or_7_out, ledbar_8_p1[11]);
  or or_9 (or_9_out, or_8_out, ledbar_8_p1[10]);
  or or_10 (or_10_out, or_9_out, ledbar_8_p1[9]);
  Multiplexer #(.width(16)) multiplexer_9 (.in0(and_8_out), .in1(adder_8_out), .out(multiplexer_9_out), .sel(in_49));
  or or_11 (or_11_out, or_10_out, ledbar_8_p1[8]);
  or or_12 (or_12_out, ledbar_8_p1[7], or_17_out);
  or or_13 (or_13_out, or_11_out, or_12_out);
  Multiplexer #(.width(16)) multiplexer_10 (.in0(multiplexer_9_out), .in1(not_6_out), .out(ledbar_8_p1), .sel(in_50));
  assign not_6_out = ~multiplexer_9_out;  // NOT_Gate not_6, 16 bits wide
  or or_14 (or_14_out, ledbar_8_p1[3], or_19_out);
  or or_15 (or_15_out, ledbar_8_p1[4], or_14_out);
  or or_16 (or_16_out, ledbar_8_p1[5], or_15_out);
  or or_17 (or_17_out, ledbar_8_p1[6], or_16_out);
  LED led_17 (.in(or_3_out));
  LED led_18 (.in(or_13_out));
  or or_18 (or_18_out, ledbar_8_p1[1], ledbar_8_p1[0]);
  or or_19 (or_19_out, ledbar_8_p1[2], or_18_out);
  Clock clock_1 (.out(clock_1_out));
  not not_7 (not_7_out, Data_Flip_Flop);
  Multiplexer #(.width(16)) multiplexer_11 (
    .in0(register_17_q), .in1(adder_9_out), .out(multiplexer_11_out), .sel(in_60));
  Adder #(.width(16)) adder_9 (.a(16'h1), .b(register_17_q), .out(adder_9_out));  // open: cin, cout
  nand nand_16 (nand_16_out, SR_Flip_Flop, clock_1_out);
  nand nand_17 (nand_17_out, clock_1_out, in_11);
  Clock clock_2 (.out(clock_2_out));
  D_Flip_Flop d_ff_1 (.D(multiplexer_12_out), .clk(clock_3_out), .Q(d_ff_1_q));  // open: Qn, preset, reset
  Multiplexer multiplexer_12 (.in0(d_ff_1_q), .in1(in_27), .out(multiplexer_12_out), .sel(in_28));
  Clock clock_3 (.out(clock_3_out));
  Clock clock_4 (.out(clock_4_out));
  Multiplexer #(.width(16)) multiplexer_13 (
    .in0(multiplexer_11_out), .in1(in_59), .out(multiplexer_13_out), .sel(in_61));
  or or_20 (or_20_out, in_60, in_61);
  nand nand_18 (nand_18_out, nand_16_out, nand_19_out);
  nand nand_19 (nand_19_out, nand_18_out, nand_17_out);
  nand nand_20 (nand_20_out, Data_Flip_Flop, clock_2_out);
  nand nand_21 (nand_21_out, clock_2_out, not_7_out);
  // LedBar #(.inputtype("row"), .matrixcols(16)) ledbar_9: pin names not known; wires that end beside it: multiplexer_12_out, ledbar_9_p2
  Register #(.width(1)) register_1 (.D(in_31[0]), .en(in_32), .clk(clock_4_out), .Q(ledbar_9_p2[0]));  // open: clr
  Register #(.width(1)) register_2 (.D(in_31[1]), .en(in_32), .clk(clock_4_out), .Q(ledbar_9_p2[1]));  // open: clr
  Register #(.width(1)) register_3 (.D(in_31[2]), .en(in_32), .clk(clock_4_out), .Q(ledbar_9_p2[2]));  // open: clr
  Register #(.width(1)) register_4 (.D(in_31[3]), .en(in_32), .clk(clock_4_out), .Q(ledbar_9_p2[3]));  // open: clr
  Register #(.width(1)) register_5 (.D(in_31[4]), .en(in_32), .clk(clock_4_out), .Q(ledbar_9_p2[4]));  // open: clr
  Register #(.width(1)) register_6 (.D(in_31[5]), .en(in_32), .clk(clock_4_out), .Q(ledbar_9_p2[5]));  // open: clr
  Register #(.width(1)) register_7 (.D(in_31[6]), .en(in_32), .clk(clock_4_out), .Q(ledbar_9_p2[6]));  // open: clr
  Register #(.width(1)) register_8 (.D(in_31[7]), .en(in_32), .clk(clock_4_out), .Q(ledbar_9_p2[7]));  // open: clr
  Register #(.width(1)) register_9 (.D(in_31[8]), .en(in_32), .clk(clock_4_out), .Q(ledbar_9_p2[8]));  // open: clr
  Register #(.width(1)) register_10 (.D(in_31[9]), .en(in_32), .clk(clock_4_out), .Q(ledbar_9_p2[9]));  // open: clr
  Register #(.width(1)) register_11 (.D(in_31[10]), .en(in_32), .clk(clock_4_out), .Q(ledbar_9_p2[10]));  // open: clr
  Register #(.width(1)) register_12 (.D(in_31[11]), .en(in_32), .clk(clock_4_out), .Q(ledbar_9_p2[11]));  // open: clr
  Register #(.width(1)) register_13 (.D(in_31[12]), .en(in_32), .clk(clock_4_out), .Q(ledbar_9_p2[12]));  // open: clr
  Register #(.width(1)) register_14 (.D(in_31[13]), .en(in_32), .clk(clock_4_out), .Q(ledbar_9_p2[13]));  // open: clr
  Register #(.width(1)) register_15 (.D(in_31[14]), .en(in_32), .clk(clock_4_out), .Q(ledbar_9_p2[14]));  // open: clr
  Register #(.width(1)) register_16 (.D(in_31[15]), .en(in_32), .clk(clock_4_out), .Q(ledbar_9_p2[15]));  // open: clr
  Register #(.width(16)) register_17 (
    .D(multiplexer_14_out), .en(or_21_out), .clk(clock_5_out), .Q(register_17_q));  // open: clr
  Clock clock_5 (.out(clock_5_out));
  Multiplexer #(.width(16)) multiplexer_14 (
    .in0(multiplexer_13_out), .in1({16{1'b0}}), .out(multiplexer_14_out), .sel(in_62));
  or or_21 (or_21_out, or_20_out, in_62);
  LED led_19 (.in(nand_18_out));
  LED led_20 (.in(nand_19_out));
  nand nand_22 (nand_22_out, nand_20_out, nand_23_out);
  LED led_21 (.in(nand_22_out));
  nand nand_23 (nand_23_out, nand_22_out, nand_21_out);
  LED led_22 (.in(nand_23_out));
  LED led_23 (.in(d_ff_1_q));
  // LedBar #(.inputtype("row"), .matrixcols(16)) ledbar_10: pin names not known; wires that end beside it: register_17_q, ledbar_10_p2
  Hex_Digit_Display hex_digit_display_1 (.value(register_17_q[15:12]));  // open: dp
  Hex_Digit_Display hex_digit_display_2 (.value(register_17_q[11:8]));  // open: dp
  Hex_Digit_Display hex_digit_display_3 (.value(register_17_q[7:4]));  // open: dp
  Hex_Digit_Display hex_digit_display_4 (.value(register_17_q[3:0]));  // open: dp
  Demultiplexer #(.select(3)) demultiplexer_5 (
    .out0(demultiplexer_5_out0), .out1(demultiplexer_5_out1), .out2(demultiplexer_5_out2),
    .out3(demultiplexer_5_out3), .out4(demultiplexer_5_out4), .out5(demultiplexer_5_out5),
    .out6(demultiplexer_5_out6), .out7(demultiplexer_5_out7), .in(in_13), .sel(in_14));
  // LedBar #(.inputtype("row"), .matrixcols(16)) ledbar_11: pin names not known; wires that end beside it: ledbar_11_p1
  Demultiplexer #(.select(3)) demultiplexer_6 (
    .out0(demultiplexer_6_out0), .out1(demultiplexer_6_out1), .out2(demultiplexer_6_out2),
    .out3(demultiplexer_6_out3), .out4(demultiplexer_6_out4), .out5(demultiplexer_6_out5),
    .out6(demultiplexer_6_out6), .out7(demultiplexer_6_out7), .in(in_41), .sel(in_46[5:3]));
  // LedBar #(.inputtype("row"), .matrixcols(16)) ledbar_12: pin names not known; wires that end beside it: ledbar_12_p1
  Clock clock_6 (.out(clock_6_out));
  Register #(.width(16)) register_18 (
    .D(in_6), .en(demultiplexer_5_out0), .clk(clock_6_out), .Q(register_18_q));  // open: clr
  Register #(.width(16)) register_19 (
    .D(in_6), .en(demultiplexer_5_out1), .clk(clock_6_out), .Q(register_19_q));  // open: clr
  Register #(.width(16)) register_20 (
    .D(in_6), .en(demultiplexer_5_out2), .clk(clock_6_out), .Q(register_20_q));  // open: clr
  Register #(.width(16)) register_21 (
    .D(in_6), .en(demultiplexer_5_out3), .clk(clock_6_out), .Q(register_21_q));  // open: clr
  Register #(.width(16)) register_22 (
    .D(in_6), .en(demultiplexer_5_out4), .clk(clock_6_out), .Q(register_22_q));  // open: clr
  Register #(.width(16)) register_23 (
    .D(in_6), .en(demultiplexer_5_out5), .clk(clock_6_out), .Q(register_23_q));  // open: clr
  Register #(.width(16)) register_24 (
    .D(in_6), .en(demultiplexer_5_out6), .clk(clock_6_out), .Q(register_24_q));  // open: clr
  Register #(.width(16)) register_25 (
    .D(in_6), .en(demultiplexer_5_out7), .clk(clock_6_out), .Q(register_25_q));  // open: clr
  Clock clock_7 (.out(clock_7_out));
  RAM #(.addrWidth(3), .dataWidth(16)) ram_1 (
    .addr(in_46[2:0]), .we(demultiplexer_6_out0), .clk(clock_7_out), .din(in_37), .dout(ram_1_dout));  // open: oe
  RAM #(.addrWidth(3), .dataWidth(16)) ram_2 (
    .addr(in_46[2:0]), .we(demultiplexer_6_out1), .clk(clock_7_out), .din(in_37), .dout(ram_2_dout));  // open: oe
  RAM #(.addrWidth(3), .dataWidth(16)) ram_3 (
    .addr(in_46[2:0]), .we(demultiplexer_6_out2), .clk(clock_7_out), .din(in_37), .dout(ram_3_dout));  // open: oe
  RAM #(.addrWidth(3), .dataWidth(16)) ram_4 (
    .addr(in_46[2:0]), .we(demultiplexer_6_out3), .clk(clock_7_out), .din(in_37), .dout(ram_4_dout));  // open: oe
  Multiplexer #(.select(3), .width(16)) multiplexer_15 (
    .in0(register_18_q), .in1(register_19_q), .in2(register_20_q), .in3(register_21_q), .in4(register_22_q),
    .in5(register_23_q), .in6(register_24_q), .in7(register_25_q), .out(ledbar_12_p1), .sel(in_14));
  RAM #(.addrWidth(3), .dataWidth(16)) ram_5 (
    .addr(in_46[2:0]), .we(demultiplexer_6_out4), .clk(clock_7_out), .din(in_37), .dout(ram_5_dout));  // open: oe
  RAM #(.addrWidth(3), .dataWidth(16)) ram_6 (
    .addr(in_46[2:0]), .we(demultiplexer_6_out5), .clk(clock_7_out), .din(in_37), .dout(ram_6_dout));  // open: oe
  RAM #(.addrWidth(3), .dataWidth(16)) ram_7 (
    .addr(in_46[2:0]), .we(demultiplexer_6_out6), .clk(clock_7_out), .din(in_37), .dout(ram_7_dout));  // open: oe
  RAM #(.addrWidth(3), .dataWidth(16)) ram_8 (
    .addr(in_46[2:0]), .we(demultiplexer_6_out7), .clk(clock_7_out), .din(in_37), .dout(ram_8_dout));  // open: oe
  Multiplexer #(.select(3), .width(16)) multiplexer_16 (
    .in0(ram_1_dout), .in1(ram_2_dout), .in2(ram_3_dout), .in3(ram_4_dout), .in4(ram_5_dout),
    .in5(ram_6_dout), .in6(ram_7_dout), .in7(ram_8_dout), .out(ledbar_11_p1), .sel(in_46[5:3]));
  not not_8 (not_8_out, or_34_out);
  not not_9 (not_9_out, or_25_out);
  and and_9 (and_9_out, not_8_out, not_9_out);
  and and_10 (and_10_out, and_9_out, in_57[0]);
  Demultiplexer demultiplexer_7 (.out0(demultiplexer_7_out0), .out1(demultiplexer_7_out1), .in(in_23), .sel(in_17[14]));
  not not_10 (not_10_out, in_57[15]);
  and and_11 (and_11_out, or_34_out, in_57[1]);
  or or_22 (or_22_out, and_10_out, and_11_out);
  or or_23 (or_23_out, or_22_out, and_13_out);
  Demultiplexer demultiplexer_8 (
    .out0(demultiplexer_8_out0), .out1(demultiplexer_8_out1), .in(demultiplexer_7_out1), .sel(in_17[13]));
  or or_24 (or_24_out, not_10_out, in_57[5]);
  and and_12 (and_12_out, in_57[4], in_57[15]);
  Multiplexer #(.width(16)) multiplexer_17 (
    .in0(register_28_q), .in1({16{1'b0}}), .out(multiplexer_17_out), .sel(in_57[11]));
  Multiplexer #(.width(16)) multiplexer_18 (
    .in0(multiplexer_25_out), .in1({16{1'b0}}), .out(multiplexer_18_out), .sel(in_57[9]));
  or or_25 (or_25_out, 1'b0, ledbar_15_p1[15]);
  LED led_24 (.in(or_25_out));
  and and_13 (and_13_out, or_25_out, in_57[2]);
  Register #(.width(16)) register_26 (.en(demultiplexer_8_out1), .clk(clock_8_out), .Q(register_26_q));  // open: D, clr
  // LedBar #(.inputtype("row"), .matrixcols(1)) ledbar_13: pin names not known; wires that end beside it: ledbar_13_p1
  and and_14 (ledbar_13_p1, in_57[15], in_57[3]);
  Multiplexer #(.width(16)) multiplexer_19 (
    .in0(multiplexer_17_out), .in1(not_11_out), .out(multiplexer_19_out), .sel(in_57[10]));
  assign not_11_out = ~multiplexer_17_out;  // NOT_Gate not_11, 16 bits wide
  Multiplexer #(.width(16)) multiplexer_20 (
    .in0(multiplexer_18_out), .in1(not_12_out), .out(multiplexer_20_out), .sel(in_57[8]));
  assign not_12_out = ~multiplexer_18_out;  // NOT_Gate not_12, 16 bits wide
  or or_26 (or_26_out, ledbar_15_p1[15], ledbar_15_p1[14]);
  or or_27 (or_27_out, or_26_out, ledbar_15_p1[13]);
  Clock clock_8 (.out(clock_8_out));
  RAM #(.addrWidth(14), .dataWidth(16)) ram_9 (
    .addr(in_17[13:0]), .we(demultiplexer_7_out0), .clk(clock_8_out), .din(in_8), .dout(ram_9_dout));  // open: oe
  RAM #(.addrWidth(13), .dataWidth(16)) ram_10 (
    .addr(in_17[12:0]), .we(demultiplexer_8_out0), .clk(clock_8_out), .din(in_8), .dout(ram_10_dout));  // open: oe
  Adder #(.width(16)) adder_10 (.a(multiplexer_19_out), .b(multiplexer_20_out), .out(adder_10_out));  // open: cin, cout
  or or_28 (or_28_out, or_27_out, ledbar_15_p1[12]);
  or or_29 (or_29_out, or_28_out, ledbar_15_p1[11]);
  or or_30 (or_30_out, or_29_out, ledbar_15_p1[10]);
  or or_31 (or_31_out, or_30_out, ledbar_15_p1[9]);
  Counter #(.max('hffff), .width(16)) counter_1 (
    .clr(in_63), .load(or_23_out), .up(1'b1), .count(1'b1), .D({register_27_q[15], ledbar_17_p1}),
    .Q(counter_1_q));  // open: clk, carry
  // LedBar #(.inputtype("row"), .matrixcols(16)) ledbar_14: pin names not known; wires that end beside it: ledbar_14_p1
  // LedBar #(.inputtype("row"), .matrixcols(16)) ledbar_15: pin names not known; wires that end beside it: ledbar_15_p1
  // LedBar #(.inputtype("row"), .matrixcols(15)) ledbar_16: pin names not known; wires that end beside it: counter_1_q[14:0]
  // LedBar #(.inputtype("row"), .matrixcols(15)) ledbar_17: pin names not known; wires that end beside it: ledbar_17_p1
  Multiplexer #(.width(16)) multiplexer_21 (
    .in0(ledbar_15_p1), .in1(in_57), .out(multiplexer_21_out), .sel(not_10_out));
  assign and_15_out = multiplexer_19_out & multiplexer_20_out;  // AND_Gate and_15, 16 bits wide
  Multiplexer #(.width(16)) multiplexer_22 (
    .in0(and_15_out), .in1(adder_10_out), .out(multiplexer_22_out), .sel(in_57[7]));
  or or_32 (or_32_out, or_31_out, ledbar_15_p1[8]);
  or or_33 (or_33_out, ledbar_15_p1[7], or_38_out);
  or or_34 (or_34_out, or_32_out, or_33_out);
  Register #(.width(16)) register_27 (
    .D(multiplexer_21_out), .en(or_24_out), .Q({register_27_q[15], ledbar_17_p1}));  // open: clk, clr
  Register #(.width(16)) register_28 (.D(ledbar_15_p1), .en(and_12_out), .Q(register_28_q));  // open: clk, clr
  assign not_13_out = ~multiplexer_22_out;  // NOT_Gate not_13, 16 bits wide
  or or_35 (or_35_out, ledbar_15_p1[3], or_40_out);
  or or_36 (or_36_out, ledbar_15_p1[4], or_35_out);
  or or_37 (or_37_out, ledbar_15_p1[5], or_36_out);
  or or_38 (or_38_out, ledbar_15_p1[6], or_37_out);
  LED led_25 (.in(or_34_out));
  Multiplexer #(.width(16)) multiplexer_23 (
    .in0(multiplexer_22_out), .in1(not_13_out), .out(ledbar_15_p1), .sel(in_57[6]));
  or or_39 (or_39_out, ledbar_15_p1[1], ledbar_15_p1[0]);
  or or_40 (or_40_out, ledbar_15_p1[2], or_39_out);
  Multiplexer #(.width(16)) multiplexer_24 (
    .in0(ram_10_dout), .in1(register_26_q), .out(multiplexer_24_out), .sel(in_17[13]));
  Multiplexer #(.width(16)) multiplexer_25 (
    .in0({register_27_q[15], ledbar_17_p1}), .in1(in_52), .out(multiplexer_25_out), .sel(in_57[12]));
  Multiplexer #(.width(16)) multiplexer_26 (
    .in0(ram_9_dout), .in1(multiplexer_24_out), .out(ledbar_14_p1), .sel(in_17[14]));

  // Notes on the sheet:
  //   AND
  //   NOT
  //   OR
  //   MUX4WAY16
  //   DeMUX4WAY16
  //   Chapter 1 - Inception
  //   XOR
  //   MUX
  //   AND
  //   OR
  //   16-bit ALU
  //   Half Adder
  //   Multibit Adders
  //   4-bit Adder
  //   Chapter 2 - Elegance
  //   1-Bit Register
  //   16-Bit Register
  //   Program Counter
  //   Chapter 3 - Remember
  //   RAM8
  //   RAM64
endmodule
